# Fritzing sketch spreadometer v3_12 (saved by Fritzing 0.9.0b)
stripboards: 2

parts:
  Part1 = Arduino Nano (Rev3.0)
  R1 = Resistor [tolerance=±5% resistance=220 package=THT]
  R2 = Resistor [tolerance=±5% resistance=220 package=THT]
  R3 = Resistor [tolerance=±5% resistance=220 package=THT]
  LED1 = RGB LED (com. cathode, rgb) [package="5 mm [THT]"]
  J1 = Basic Servo
  R4 = Resistor [tolerance=±5% resistance=1M package=THT]
  U1 = CAPSENSE_PAD [package=capsense_pad]

nets:
  GND: Part1.GND, LED1.common_cathode, J1.gnd
  N1: Part1.D2, R4.Pin_1, U1.RES
  N2: Part1.D4, R4.Pin_0
  N3: Part1.D6, J1.pulse
  N4: Part1.D9, R1.Pin_0
  N5: Part1.D10, R3.Pin_0
  N6: Part1.D11/MOSI, R2.Pin_0
  5V: Part1.5V, J1.vcc
  N7: R1.Pin_1, LED1.green_anode
  N8: R2.Pin_1, LED1.red_anode
  N9: R3.Pin_1, LED1.blue_anode
